# Fritzing sketch RS_485_DMX512_Controller_Teil_2 (saved by Fritzing 0.9.3b)

parts:
  Bauteil1 = Arduino Uno (Rev3)  # not connected
  Bauteil5 = RS485 Shield
  XLR1 = XLR3_NCFAH2 [package=xlr3_nc3fah2]

nets:
  N1: Bauteil5.GND, XLR1.1
  N2: Bauteil5.A, XLR1.G
  N3: Bauteil5.B, XLR1.3
