# Fritzing sketch RS_485_DMX512_Controller_Teil_3 (saved by Fritzing 0.9.3b)
breadboards: 1

parts:
  KY-004_Button_Module2 = KY-004 Button Module
  KY-004_Button_Module3 = KY-004 Button Module
  KY-004_Button_Module4 = KY-004 Button Module
  Nano_V1 = Nano V3

nets:
  N1: KY-004_Button_Module2.Vin, Nano_V1.D4
  N2: KY-004_Button_Module2.-, KY-004_Button_Module3.-, KY-004_Button_Module4.-, Nano_V1.GND
  N3: KY-004_Button_Module3.Vin, Nano_V1.D3
  N4: KY-004_Button_Module4.Vin, Nano_V1.D2

custom parts:
  KY-004 Button Module: Universal Button Module for direct use with Arduino, Raspberry & Co. Operating Voltage 3.3 V - 5 V Usual high quality and fast delivery directly from Germany by order AZ Delivery Of course, you will receive when you purchase through AZDelivery fully automatically and guarantees a Invoice incl. VAT and according to German Standards Guaranteed ROHS compliance by purchase from the German trader
  Nano V3: Can be used universally thanks to a compact design! By 14 digital in - and outputs and 6 analog inputs on the Nano V3 can also be used for larger projects! Thanks to the ATmega328 micro-controller, as well as more sophisticated programs to be executable! By Arduino compatibility in the Arduino IDE programmable! With FTDI Chip! Usual high quality and fast delivery directly from Germany by order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
